// Logisim project single_cycle.circ as structural Verilog: 6 circuits, main circuit main
module main (
);

  wire instr_decoder_1_aa, instr_decoder_1_alu_in, instr_decoder_1_ba, instr_decoder_1_da,
       instr_decoder_1_ma, instr_decoder_1_mb, multiplexer_1_out, multiplexer_2_out, register_file_1_a,
       register_file_1_b;

  PC pc_1 ();  // open: in_1, out_2
  instr_decoder instr_decoder_1 (
    .aa(instr_decoder_1_aa), .ba(instr_decoder_1_ba), .da(instr_decoder_1_da),
    .alu_in(instr_decoder_1_alu_in), .Ma(instr_decoder_1_ma), .Mb(instr_decoder_1_mb));  // open: instruction, Mcomp, reg_write, mem_write
  Multiplexer multiplexer_1 (.in0(register_file_1_a), .out(multiplexer_1_out), .sel(instr_decoder_1_ma));  // open: in1
  alu alu_1 (.alu_in(instr_decoder_1_alu_in), .in1(multiplexer_1_out), .in2(multiplexer_2_out));
  compare compare_1 (.com1(multiplexer_1_out), .com2(multiplexer_2_out));  // open: comp_in
  register_file register_file_1 (
    .aa(instr_decoder_1_aa), .ba(instr_decoder_1_ba), .da(instr_decoder_1_da), .A(register_file_1_a),
    .B(register_file_1_b));
  Multiplexer multiplexer_2 (.in0(register_file_1_b), .out(multiplexer_2_out), .sel(instr_decoder_1_mb));  // open: in1
endmodule

module PC (
  input  in_1,
  output out_2
);
endmodule

module instr_decoder (
  input  [31:0] instruction,
  output aa,
  output ba,
  output da,
  output alu_in,
  output Mcomp,
  output Ma,
  output Mb,
  output reg_write,
  output mem_write
);
endmodule

module register_file (
  input  aa,
  input  ba,
  input  da,
  output A,
  output B
);
endmodule

module alu (
  input  alu_in,
  input  in1,
  input  in2
);
endmodule

module compare (
  input  com1,
  input  com2,
  input  comp_in
);
endmodule
